# Fritzing sketch infoDome (saved by Fritzing 0.9.2b)

parts:
  Yun_Mini = Arduino Yun
  part = Barometric Pressure Sensor - BMP085 Breakout
  X1 = USB Connectors [package=usb-a-h]
  Sharp_GP2Y0A21YK = Infrared Proximity Sensor
  JP1 = Header 6 [package=molex-1x6_lock]
  part_2 = Real Time Clock Module - DS1307 RTC Breakout Board

nets:
  N1: Yun_Mini.A1, Sharp_GP2Y0A21YK.Vout
  N2: Yun_Mini.A5/SCL, part.SCL, part_2.SCL
  N3: Yun_Mini.ICSP_MISO, JP1.5
  5V: Yun_Mini.5V, part.VCC, Sharp_GP2Y0A21YK.Vcc, JP1.1, part_2.5V
  N4: Yun_Mini.ICSP_SCK, Yun_Mini.D13/SCK, JP1.6
  N5: Yun_Mini.ICSP_MOSI, Yun_Mini.D11_PWM/MOSI, JP1.3
  GND: Yun_Mini.GND, part.GND, X1.GND, Sharp_GP2Y0A21YK.GND, JP1.2, part_2.GND
  N6: Yun_Mini.D10_PWM/SS, JP1.4
  N7: Yun_Mini.D2/SDA, Yun_Mini.D2, part.SDA, part_2.SDA
  N8: Yun_Mini.VIN, X1.D+

notes:
  Nixie Tube Pins
  1 5V
  2 GND
  3 DIN
  4 OE
  5 ST
  6 SH
